// Logisim project comp.circ as structural Verilog: 1 circuit, main circuit main
module main (
);

  wire A_In, A_Out, Addr_H_In, Addr_L_In, Addr_Out, Addr_To_Cnt, and_2_out, and_3_out, CLK, clock_1_out,
       CNT_En, Cnt_H_In, Cnt_L_In, d_ff_1_q, d_ff_1_qn, D_In, decoder_1_out0, decoder_1_out1, decoder_1_out2,
       HLT, Inst_In, Mic_RST, nor_1_out, nor_3_out, not_1_out, not_2_out, not_3_out, P_Cnt_Lo_carry, SP_In,
       SP_Out, Write, X_In, X_Out, Y_In, Y_Out;
  wire [3:0] Micro_q;
  wire [6:0] keyboard_1_data;
  wire [7:0] A_q, Addr_Hi_q, Addr_Lo_q, controlled_buffer_6_out, Data, Inst_q, multiplexer_1_out,
       multiplexer_2_out, multiplexer_3_out, P_Cnt_Hi_q, P_Cnt_Lo_q, ram_1_data, random_1_out, SP_q, X_q, Y_q;
  wire [7:7] keyboard_1_avail;
  wire [15:0] multiplexer_4_out;
  wire [23:19] rom_2_data;

  Clock clock_1 (.out(clock_1_out));
  D_Flip_Flop d_ff_1 (.clk(CLK), .D(d_ff_1_qn), .Q(d_ff_1_q), .Qn(d_ff_1_qn), .en(d_ff_1_qn));  // open: preset, reset
  and and_1 (CLK, clock_1_out, ~HLT);  // AND_Gate
  nor nor_1 (nor_1_out, multiplexer_4_out[14], multiplexer_4_out[15]);
  Register Addr_Lo (.D(Data), .en(Addr_L_In), .Q(Addr_Lo_q), .clk(CLK));  // open: clr
  Multiplexer #(.width(8), .enable("false")) multiplexer_1 (
    .in0(Data), .in1({8{1'b1}}), .out(multiplexer_1_out), .sel(d_ff_1_qn));
  not not_1 (not_1_out, d_ff_1_qn);
  not not_2 (not_2_out, Write);
  Register Addr_Hi (.D(Data), .en(Addr_H_In), .Q(Addr_Hi_q), .clk(CLK));  // open: clr
  Counter #(.width(4), .max('hf), .trigger("falling")) Micro (
    .Q(Micro_q), .clk(CLK), .clr(Mic_RST));  // open: load, D, count, carry
  Register Inst (.D(multiplexer_1_out), .en(Inst_In), .Q(Inst_q), .clk(CLK));  // open: clr
  assign Inst_In = d_ff_1_qn ? d_ff_1_qn : 1'bz;  // Controlled_Buffer controlled_buffer_1
  assign Addr_Out = d_ff_1_qn ? d_ff_1_qn : 1'bz;  // Controlled_Buffer controlled_buffer_2
  assign CNT_En = d_ff_1_qn ? not_1_out : 1'bz;  // Controlled_Buffer controlled_buffer_3
  RAM #(.addrWidth(14)) ram_1 (
    .addr(multiplexer_4_out[13:0]), .data(ram_1_data), .sel(nor_1_out), .clk(CLK), .ld(not_2_out), .clr(1'b0));
  ROM #(.addrWidth(15)) rom_1 (.addr(multiplexer_4_out[14:0]), .data(ram_1_data), .sel(multiplexer_4_out[15]));
  assign ram_1_data = not_3_out ? Data : 8'bz;  // Controlled_Buffer controlled_buffer_4
  not not_3 (not_3_out, D_In);
  assign Data = D_In ? ram_1_data : 8'bz;  // Controlled_Buffer controlled_buffer_5
  Multiplexer #(.width(8), .enable("false")) multiplexer_2 (
    .in0(Data), .in1(Addr_Lo_q), .out(multiplexer_2_out), .sel(Addr_To_Cnt));
  // Probe on ram_1_data
  // Probe on multiplexer_4_out
  Multiplexer #(.width(8), .enable("false")) multiplexer_3 (
    .in0(Data), .in1(Addr_Hi_q), .out(multiplexer_3_out), .sel(Addr_To_Cnt));
  ROM #(.addrWidth(12), .dataWidth(24)) rom_2 (
    .addr({Inst_q, Micro_q}),
    .data({rom_2_data, D_In, Addr_To_Cnt, SP_Out, Y_Out, Y_In, X_Out, X_In, Write, SP_In, CNT_En, A_Out, A_In, Inst_In, Addr_H_In, Addr_L_In, Cnt_H_In, Cnt_L_In, Mic_RST, Addr_Out}),
    .sel(d_ff_1_q));
  nor nor_2 (HLT, Addr_Out, Mic_RST, Cnt_L_In, Cnt_H_In, Addr_L_In, Addr_H_In, Inst_In, A_In, A_Out, CNT_En, SP_In, Write, X_Out, Y_In, Y_Out, SP_Out, Addr_To_Cnt, D_In, rom_2_data[19], rom_2_data[20], rom_2_data[21], rom_2_data[22], rom_2_data[23], X_In);
  Counter #(.trigger("falling")) P_Cnt_Lo (
    .load(Cnt_L_In), .D(multiplexer_2_out), .count(CNT_En), .Q(P_Cnt_Lo_q), .carry(P_Cnt_Lo_carry), .clk(CLK));  // open: clr
  nor nor_3 (nor_3_out, multiplexer_4_out[15], multiplexer_4_out[8], multiplexer_4_out[9], multiplexer_4_out[10], multiplexer_4_out[11]);
  Counter #(.trigger("falling")) P_Cnt_Hi (
    .load(Cnt_H_In), .D(multiplexer_3_out), .count(P_Cnt_Lo_carry), .Q(P_Cnt_Hi_q), .clk(CLK));  // open: carry, clr
  and and_2 (and_2_out, nor_3_out, multiplexer_4_out[12], multiplexer_4_out[13], multiplexer_4_out[14]);
  Multiplexer #(.width(16), .disabled(0), .enable("false")) multiplexer_4 (
    .in0({P_Cnt_Hi_q, P_Cnt_Lo_q}), .in1({Addr_Hi_q, Addr_Lo_q}), .out(multiplexer_4_out), .sel(Addr_Out));
  Decoder #(.select(2), .disabled(0)) decoder_1 (
    .out0(decoder_1_out0), .out1(decoder_1_out1), .out2(decoder_1_out2), .sel(multiplexer_4_out[1:0]),
    .en(and_2_out));  // open: out3
  and and_3 (and_3_out, CLK, decoder_1_out0);
  assign controlled_buffer_6_out = decoder_1_out0 ? ram_1_data : 8'bz;  // Controlled_Buffer controlled_buffer_6
  Keyboard keyboard_1 (
    .clk(CLK), .re(decoder_1_out1), .avail(keyboard_1_avail[7]), .data(keyboard_1_data));  // open: clr
  assign ram_1_data = decoder_1_out1 ? {keyboard_1_avail[7], keyboard_1_data} : 8'bz;  // Controlled_Buffer controlled_buffer_7
  Random random_1 (.clk(CLK), .next(decoder_1_out2), .out(random_1_out));  // open: clr
  assign ram_1_data = decoder_1_out2 ? random_1_out : 8'bz;  // Controlled_Buffer controlled_buffer_8
  TTY tty_1 (
    .data(controlled_buffer_6_out[6:0]), .clk(and_3_out), .we(decoder_1_out0),
    .clr(controlled_buffer_6_out[7]));
  Joystick joystick_1 ();  // open: x, y
  DotMatrix #(.matrixcols(32), .matrixrows(32)) dotmatrix_1 ();  // open: col0, col1, col2, col3, col4, col5, col6, col7, col8, col9, col10, col11, col12, col13, col14, col15, col16, col17, col18, col19, col20, col21, col22, col23, col24, col25, col26, col27, col28, col29, col30, col31
  assign Data = A_Out ? A_q : 8'bz;  // Controlled_Buffer controlled_buffer_9
  Register A (.D(Data), .en(A_In), .Q(A_q), .clk(CLK));  // open: clr
  assign Data = X_Out ? X_q : 8'bz;  // Controlled_Buffer controlled_buffer_10
  Register X (.D(Data), .en(X_In), .Q(X_q), .clk(CLK));  // open: clr
  Register Y (.D(Data), .en(Y_In), .Q(Y_q), .clk(CLK));  // open: clr
  assign Data = Y_Out ? Y_q : 8'bz;  // Controlled_Buffer controlled_buffer_11
  assign Data = SP_Out ? SP_q : 8'bz;  // Controlled_Buffer controlled_buffer_12
  Register SP (.D(Data), .en(SP_In), .Q(SP_q), .clk(CLK));  // open: clr

  // Notes on the sheet:
  //   contents of rom_1 (hex, n*v repeats v):
  //   a9 53 8d 0 70 aa 32758*ff 0 80
  //   contents of rom_2 (hex, n*v repeats v):
  //   2256*0 40240 40210 40220 901 2 443*0 40240 40280 2 13*0 40240 1100 2 1357*0 40040 20c 204 204 40224
  //   40010 2000c 2
endmodule
